// Logisim project RISC V Logisim Simulation.circ as structural Verilog: 16 circuits, main circuit main
// Func_7
module main (
  input  in_1,
  output [31:0] out_2,
  output [31:0] x5,
  output [31:0] x11,
  output [1:0] out_5,
  output [31:0] x6,
  output [31:0] x12,
  output [31:0] out_8,
  output [31:0] x7,
  output [31:0] x13,
  output [31:0] out_11,
  output [31:0] x8,
  output [31:0] x14,
  output [31:0] out_14,
  output [3:0] out_15,
  output [31:0] x9,
  output [31:0] x15,
  output [1:0] out_18,
  output [31:0] x10,
  output [31:0] x16,
  output [31:0] out_21,
  output [31:0] out_22,
  output [1:0] out_23
);

  wire and_1_out, B, Branch_Selector_out_4, clock_1_out, Func_7, Load, Op_B, Store, W;
  wire [2:0] Func_3;
  wire [4:0] R1_w, R2_w, Wd;
  wire [6:0] Op;
  wire [31:0] adder_1_out, I, multiplexer_2_out, multiplexer_3_out, ram_1_data, register_1_q, rs1, rs2, S,
       SB, U, UJ;
  wire [31:25] rom_1_data;

  Multiplexer #(.select(2), .width(32), .enable("false")) multiplexer_1 (
    .in0(adder_1_out), .in1(UJ), .in2(out_2), .in3(multiplexer_2_out), .out(out_8), .sel(out_5));
  Register #(.width(32)) register_1 (.D(out_8), .Q(register_1_q), .clk(clock_1_out), .clr(in_1));  // open: en
  Clock clock_1 (.out(clock_1_out));
  Branch_Selector Branch_Selector (.out_4(Branch_Selector_out_4), .Rs1(rs1), .Rs2(rs2), .in_3(Func_3));
  Adder #(.width(32)) adder_1 (.a(register_1_q), .b(32'h4), .out(adder_1_out));  // open: cin, cout
  Imm_Generation Imm_Generation (
    .Instruction_Memory({rom_1_data[31], Func_7, rom_1_data[29:25], R2_w, R1_w, Func_3, Wd, Op}),
    .PC(register_1_q), .I_Type(I), .S_Type(S), .SB_Type(SB), .U_Type(U), .UJ_Type(UJ));
  Multiplexer #(.width(32), .enable("false")) multiplexer_2 (
    .in0(adder_1_out), .in1(SB), .out(multiplexer_2_out), .sel(and_1_out));
  ROM #(.addrWidth(12), .dataWidth(32)) rom_1 (
    .addr(register_1_q[13:2]), .data({rom_1_data[31], Func_7, rom_1_data[29:25], R2_w, R1_w, Func_3, Wd, Op}));  // open: sel
  and and_1 (and_1_out, B, Branch_Selector_out_4);
  Register_File Register_File (
    .Instruction_Memory(out_11), .Rs2(rs2), .EN(W), .in_3(Wd), .Source_Register_2(R2_w), .Rs1(rs1),
    .Source_Register_1(R1_w), .Clock(clock_1_out), .x5(x5), .x6(x6), .x7(x7), .x8(x8), .x11(x11), .x12(x12),
    .x13(x13), .x14(x14), .x9(x9), .x10(x10), .x15(x15), .x16(x16));
  Multiplexer #(.select(2), .width(32), .enable("false")) multiplexer_3 (
    .in0(I), .in1(S), .in2(U), .out(multiplexer_3_out), .sel(out_23));  // open: in3
  Adder #(.width(32)) adder_2 (.a(rs1), .b(I), .out(out_2));  // open: cin, cout
  Multiplexer #(.select(2), .width(32), .enable("false")) multiplexer_4 (
    .in0(rs1), .in1(adder_1_out), .in2(register_1_q), .in3({32{1'b0}}), .out(out_14), .sel(out_18));
  Multiplexer #(.width(32), .enable("false")) multiplexer_5 (
    .in0(rs2), .in1(multiplexer_3_out), .out(out_21), .sel(Op_B));
  ALU ALU (.in_1(out_15), .Operand_A(out_14), .Operand_B(out_21), .Output(out_22));
  Control_Unit Control_Unit (
    .Opcode(Op), .in_2(Func_3), .in_3(Func_7), .Write(W), .Store(Store), .Load(Load), .Branch(B),
    .Operand_A(out_18), .Operand_B(Op_B), .Immediate(out_23), .Next_PC(out_5), .ALU_Operation(out_15));
  RAM #(.addrWidth(12), .dataWidth(32), .bus("separate")) ram_1 (
    .addr(out_22[13:2]), .din(rs2), .data(ram_1_data), .str(Store), .clk(clock_1_out), .ld(Load), .clr(in_1));  // open: sel
  Multiplexer #(.width(32), .enable("false")) multiplexer_6 (.in0(out_22), .in1(ram_1_data), .out(out_11), .sel(Load));

  // Other names for the same wires on the sheet: I_S[1:0] = out_23; N_P[1:0] = out_5; O_S[3:0] = out_15;
  //   Op_A[1:0] = out_18; wb[31:0] = out_11

  // Notes on the sheet:
  //   contents of rom_1 (hex, n*v repeats v):
  //   500293 fffff317 fffff3b7 100437 fff40413 20480e7 10000ef 14000ef 552023 8067 52583 8067 13
  //   Risc V Single Cycle by Syed Sohaib Shere
endmodule

module Type_Decoder (
  input  [6:0] Instruction_Memory,
  output R_Type,
  output I_Type,
  output I_Type_2,
  output I_Type_3,
  output S_Type,
  output SB_Type,
  output U_Type,
  output U_Type_2,
  output UJ_Type
);

  Comparator #(.width(7)) comparator_1 (.a(Instruction_Memory), .b(7'b0110011), .eq(R_Type));  // open: gt, lt
  Comparator #(.width(7)) comparator_2 (.a(Instruction_Memory), .b(7'b0000011), .eq(I_Type));  // open: gt, lt
  Comparator #(.width(7)) comparator_3 (.a(Instruction_Memory), .b(7'b0010011), .eq(I_Type_2));  // open: gt, lt
  Comparator #(.width(7)) comparator_4 (.a(Instruction_Memory), .b(7'b1100111), .eq(I_Type_3));  // open: gt, lt
  Comparator #(.width(7)) comparator_5 (.a(Instruction_Memory), .b(7'b0100011), .eq(S_Type));  // open: gt, lt
  Comparator #(.width(7)) comparator_6 (.a(Instruction_Memory), .b(7'b1100011), .eq(SB_Type));  // open: gt, lt
  Comparator #(.width(7)) comparator_7 (.a(Instruction_Memory), .b(7'b0010111), .eq(U_Type));  // open: gt, lt
  Comparator #(.width(7)) comparator_8 (.a(Instruction_Memory), .b(7'b0110111), .eq(U_Type_2));  // open: gt, lt
  Comparator #(.width(7)) comparator_9 (.a(Instruction_Memory), .b(7'b1101111), .eq(UJ_Type));  // open: gt, lt
endmodule

module Imm_Generation (
  input  [31:0] Instruction_Memory,
  input  [31:0] PC,
  output [31:0] I_Type,
  output [31:0] S_Type,
  output [31:0] SB_Type,
  output [31:0] U_Type,
  output [31:0] UJ_Type
);

  wire [31:0] bit_extender_3_out, bit_extender_4_out, bit_extender_5_out;

  assign I_Type = {{20{Instruction_Memory[31]}}, Instruction_Memory[31:20]};  // Bit_Extender bit_extender_1
  assign S_Type = {{20{Instruction_Memory[31]}}, {Instruction_Memory[31:25], Instruction_Memory[11:7]}};  // Bit_Extender bit_extender_2
  assign bit_extender_3_out = {{19{Instruction_Memory[31]}}, {Instruction_Memory[31], Instruction_Memory[7], Instruction_Memory[30:25], Instruction_Memory[11:8], 1'b0}};  // Bit_Extender bit_extender_3
  assign bit_extender_4_out = {{12{Instruction_Memory[31]}}, Instruction_Memory[31:12]};  // Bit_Extender bit_extender_4
  assign bit_extender_5_out = {{11{Instruction_Memory[31]}}, {Instruction_Memory[31], Instruction_Memory[19:12], Instruction_Memory[20], Instruction_Memory[30:21], 1'b0}};  // Bit_Extender bit_extender_5
  Adder #(.width(32)) adder_1 (.a(bit_extender_3_out), .b(PC), .out(SB_Type));  // open: cin, cout
  Shifter #(.width(32)) shifter_1 (.in(bit_extender_4_out), .\dist (5'b01100), .out(U_Type));
  Adder #(.width(32)) adder_2 (.a(bit_extender_5_out), .b(PC), .out(UJ_Type));  // open: cin, cout
endmodule

module Register_File (
  input  [31:0] Instruction_Memory,
  input  EN,
  input  [4:0] in_3,
  input  [4:0] Source_Register_1,
  input  [4:0] Source_Register_2,
  input  Clock,
  output [31:0] x5,
  output [31:0] x11,
  output [31:0] x6,
  output [31:0] x12,
  output [31:0] x7,
  output [31:0] x13,
  output [31:0] x8,
  output [31:0] x14,
  output [31:0] x9,
  output [31:0] x15,
  output [31:0] x10,
  output [31:0] x16,
  output [31:0] Rs1,
  output [31:0] Rs2
);

  wire decoder_1_out1, decoder_1_out2, decoder_1_out3, decoder_1_out4, decoder_1_out5, decoder_1_out6,
       decoder_1_out7, decoder_1_out8, decoder_1_out9, decoder_1_out10, decoder_1_out11, decoder_1_out12,
       decoder_1_out13, decoder_1_out14, decoder_1_out15, decoder_1_out16, decoder_1_out17, decoder_1_out18,
       decoder_1_out19, decoder_1_out20, decoder_1_out21, decoder_1_out22, decoder_1_out23, decoder_1_out24,
       decoder_1_out25, decoder_1_out26, decoder_1_out27, decoder_1_out28, decoder_1_out29, decoder_1_out30,
       decoder_1_out31;
  wire [31:0] x1, x2, x3, x4, x17, x18, x19, x20, x21, x22, x23, x24, x25, x26, x27, x28, x30, x31;

  Decoder #(.select(5), .disabled(0)) decoder_1 (
    .out1(decoder_1_out1), .out2(decoder_1_out2), .out3(decoder_1_out3), .out4(decoder_1_out4),
    .out5(decoder_1_out5), .out6(decoder_1_out6), .out7(decoder_1_out7), .out8(decoder_1_out8),
    .out9(decoder_1_out9), .out10(decoder_1_out10), .out11(decoder_1_out11), .out12(decoder_1_out12),
    .out13(decoder_1_out13), .out14(decoder_1_out14), .out15(decoder_1_out15), .out16(decoder_1_out16),
    .out17(decoder_1_out17), .out18(decoder_1_out18), .out19(decoder_1_out19), .out20(decoder_1_out20),
    .out21(decoder_1_out21), .out22(decoder_1_out22), .out23(decoder_1_out23), .out24(decoder_1_out24),
    .out25(decoder_1_out25), .out26(decoder_1_out26), .out27(decoder_1_out27), .out28(decoder_1_out28),
    .out29(decoder_1_out29), .out30(decoder_1_out30), .out31(decoder_1_out31), .sel(in_3), .en(EN));  // open: out0
  Register #(.width(32)) register_1 (.D(Instruction_Memory), .en(decoder_1_out1), .Q(x1), .clk(Clock));  // open: clr
  Register #(.width(32)) register_2 (.D(Instruction_Memory), .en(decoder_1_out2), .Q(x2), .clk(Clock));  // open: clr
  Register #(.width(32)) register_3 (.D(Instruction_Memory), .en(decoder_1_out3), .Q(x3), .clk(Clock));  // open: clr
  Register #(.width(32)) register_4 (.D(Instruction_Memory), .en(decoder_1_out4), .Q(x4), .clk(Clock));  // open: clr
  Register #(.width(32)) register_5 (.D(Instruction_Memory), .en(decoder_1_out5), .Q(x5), .clk(Clock));  // open: clr
  Register #(.width(32)) register_6 (.D(Instruction_Memory), .en(decoder_1_out6), .Q(x6), .clk(Clock));  // open: clr
  Register #(.width(32)) register_7 (.D(Instruction_Memory), .en(decoder_1_out7), .Q(x7), .clk(Clock));  // open: clr
  Register #(.width(32)) register_8 (.D(Instruction_Memory), .en(decoder_1_out8), .Q(x8), .clk(Clock));  // open: clr
  Register #(.width(32)) register_9 (.D(Instruction_Memory), .en(decoder_1_out9), .Q(x9), .clk(Clock));  // open: clr
  Register #(.width(32)) register_10 (.D(Instruction_Memory), .en(decoder_1_out10), .Q(x10), .clk(Clock));  // open: clr
  Register #(.width(32)) register_11 (.D(Instruction_Memory), .en(decoder_1_out11), .Q(x11), .clk(Clock));  // open: clr
  Register #(.width(32)) register_12 (.D(Instruction_Memory), .en(decoder_1_out12), .Q(x12), .clk(Clock));  // open: clr
  Register #(.width(32)) register_13 (.D(Instruction_Memory), .en(decoder_1_out13), .Q(x13), .clk(Clock));  // open: clr
  Register #(.width(32)) register_14 (.D(Instruction_Memory), .en(decoder_1_out14), .Q(x14), .clk(Clock));  // open: clr
  Register #(.width(32)) register_15 (.D(Instruction_Memory), .en(decoder_1_out15), .Q(x15), .clk(Clock));  // open: clr
  Register #(.width(32)) register_16 (.D(Instruction_Memory), .en(decoder_1_out16), .Q(x16), .clk(Clock));  // open: clr
  Register #(.width(32)) register_17 (.D(Instruction_Memory), .en(decoder_1_out17), .Q(x17), .clk(Clock));  // open: clr
  Register #(.width(32)) register_18 (.D(Instruction_Memory), .en(decoder_1_out18), .Q(x18), .clk(Clock));  // open: clr
  Register #(.width(32)) register_19 (.D(Instruction_Memory), .en(decoder_1_out19), .Q(x19), .clk(Clock));  // open: clr
  Register #(.width(32)) register_20 (.D(Instruction_Memory), .en(decoder_1_out20), .Q(x20), .clk(Clock));  // open: clr
  Register #(.width(32)) register_21 (.D(Instruction_Memory), .en(decoder_1_out21), .Q(x21), .clk(Clock));  // open: clr
  Register #(.width(32)) register_22 (.D(Instruction_Memory), .en(decoder_1_out22), .Q(x22), .clk(Clock));  // open: clr
  Register #(.width(32)) register_23 (.D(Instruction_Memory), .en(decoder_1_out23), .Q(x23), .clk(Clock));  // open: clr
  Register #(.width(32)) register_24 (.D(Instruction_Memory), .en(decoder_1_out24), .Q(x24), .clk(Clock));  // open: clr
  Register #(.width(32)) register_25 (.D(Instruction_Memory), .en(decoder_1_out25), .Q(x25), .clk(Clock));  // open: clr
  Register #(.width(32)) register_26 (.D(Instruction_Memory), .en(decoder_1_out26), .Q(x26), .clk(Clock));  // open: clr
  Register #(.width(32)) register_27 (.D(Instruction_Memory), .en(decoder_1_out27), .Q(x27), .clk(Clock));  // open: clr
  Register #(.width(32)) register_28 (.D(Instruction_Memory), .en(decoder_1_out28), .Q(x28), .clk(Clock));  // open: clr
  Register #(.width(32)) register_29 (.D(Instruction_Memory), .en(decoder_1_out29), .Q(x25), .clk(Clock));  // open: clr
  Register #(.width(32)) register_30 (.D(Instruction_Memory), .en(decoder_1_out30), .Q(x30), .clk(Clock));  // open: clr
  Register #(.width(32)) register_31 (.D(Instruction_Memory), .en(decoder_1_out31), .Q(x31), .clk(Clock));  // open: clr
  Multiplexer #(.select(5), .width(32), .enable("false")) multiplexer_1 (
    .in0({32{1'b0}}), .in1(x1), .in2(x2), .in3(x3), .in4(x4), .in5(x5), .in6(x6), .in7(x7), .in8(x8),
    .in9(x9), .in10(x10), .in11(x11), .in12(x12), .in13(x13), .in14(x14), .in15(x15), .in16(x16), .in17(x17),
    .in18(x18), .in19(x19), .in20(x20), .in21(x21), .in22(x22), .in23(x23), .in24(x24), .in25(x25),
    .in26(x26), .in27(x27), .in28(x28), .in29(x25), .in30(x30), .in31(x31), .out(Rs1), .sel(Source_Register_1));
  Multiplexer #(.select(5), .width(32), .enable("false")) multiplexer_2 (
    .in0({32{1'b0}}), .in1(x1), .in2(x2), .in3(x3), .in4(x4), .in5(x5), .in6(x6), .in7(x7), .in8(x8),
    .in9(x9), .in10(x10), .in11(x11), .in12(x12), .in13(x13), .in14(x14), .in15(x15), .in16(x16), .in17(x17),
    .in18(x18), .in19(x19), .in20(x20), .in21(x21), .in22(x22), .in23(x23), .in24(x24), .in25(x25),
    .in26(x26), .in27(x27), .in28(x28), .in29(x25), .in30(x30), .in31(x31), .out(Rs2), .sel(Source_Register_2));

  // Other names for the same wires on the sheet: x29[31:0] = x25
endmodule

module Control_Decoder (
  input  R_Type,
  input  I_Type,
  input  Load,
  input  JALR,
  input  Store,
  input  Branch,
  input  Auipc,
  input  Lui,
  input  JAL,
  input  [2:0] func_3,
  input  func_7,
  output Write,
  output Branch_2,
  output Store_2,
  output Load_2,
  output [1:0] Operand_A,
  output Operand_B,
  output [1:0] Immediate_Selector,
  output [2:0] out_19,
  output [1:0] Next_PC,
  output [3:0] ALU_Operation_Selector
);

  wire or_1_out, or_2_out, or_3_out;

  or or_1 (or_1_out, Store, Load, I_Type, R_Type);
  or or_2 (or_2_out, Auipc, Lui);
  or or_3 (or_3_out, JALR, JAL);
  or or_4 (Write, I_Type, Load, JALR, R_Type, Auipc, Lui, JAL);
  Operand_A operand_a_1 (
    .jalr(or_3_out), .auipc(Auipc), .rsi(or_1_out), .zero(1'b0), .out0(Operand_A[1]), .out1(Operand_A[0]));
  or or_5 (Operand_B, I_Type, JALR, or_2_out, Store);
  Immediate_Selector immediate_selector_1 (
    .STYPE(Store), .UTYPE(or_2_out), .IType(I_Type), .a(Immediate_Selector[1]), .b(Immediate_Selector[0]));
  Next_PC_Selector next_pc_selector_1 (.SBTYPE(Branch), .JALR(JALR), .JAL(JAL), .a(Next_PC[1]), .b(Next_PC[0]));
  ALU_Operation_Selector_1 alu_operation_selector_1_1 (
    .Rtype(R_Type), .itype(I_Type), .load(Load), .jalr(JALR), .store(Store), .auipc(Auipc), .lui(Lui),
    .jal(JAL), .a(out_19[2]), .b(out_19[1]), .c(out_19[0]));
  ALU_Controller_5 alu_controller_5_1 (
    .ALU_op_2(out_19[2]), .ALU_op_1(out_19[1]), .ALU_op_0(out_19[0]), .func_7(func_7), .fun3_2(func_3[2]),
    .fun3_1(func_3[1]), .fun3_0(func_3[0]), .a(ALU_Operation_Selector[3]), .b(ALU_Operation_Selector[2]),
    .c(ALU_Operation_Selector[1]), .d(ALU_Operation_Selector[0]));

  assign Branch_2 = Branch;
  assign Load_2 = Load;
  assign Store_2 = Store;
endmodule

module Operand_A (
  input  jalr,
  input  auipc,
  input  rsi,
  input  zero,
  output out0,
  output out1
);

  wire and_2_out, and_3_out, not_1_out, not_2_out, not_3_out, not_4_out, not_5_out, not_6_out, not_7_out,
       not_8_out;

  not not_1 (not_1_out, jalr);
  and and_1 (out0, not_1_out, not_2_out);
  not not_2 (not_2_out, rsi);
  not not_3 (not_3_out, jalr);
  and and_2 (and_2_out, not_3_out, not_4_out, not_5_out);
  not not_4 (not_4_out, auipc);
  not not_5 (not_5_out, rsi);
  not not_6 (not_6_out, auipc);
  not not_7 (not_7_out, rsi);
  and and_3 (and_3_out, not_6_out, not_7_out, not_8_out);
  not not_8 (not_8_out, zero);
  or or_1 (out1, and_2_out, and_3_out);
endmodule

module Immediate_Selector (
  input  STYPE,
  input  UTYPE,
  input  IType,
  output a,
  output b
);

  wire not_1_out, not_2_out, not_3_out, not_4_out;

  not not_1 (not_1_out, STYPE);
  not not_2 (not_2_out, IType);
  not not_3 (not_3_out, UTYPE);
  not not_4 (not_4_out, IType);
  and and_1 (a, not_1_out, not_2_out);
  and and_2 (b, not_3_out, not_4_out);
endmodule

module Next_PC_Selector (
  input  SBTYPE,
  input  JALR,
  input  JAL,
  output a,
  output b
);

  or or_1 (a, JALR, SBTYPE);
  or or_2 (b, JAL, SBTYPE);
endmodule

module ALU_Operation_Selector (
  input  Rtype,
  input  itype,
  input  load,
  input  jalr,
  input  store,
  input  auipc,
  input  lui,
  input  jal,
  output a,
  output b,
  output c
);

  or or_1 (a, jal, lui, auipc, store);
  or or_2 (b, jal, lui, jalr, load);
  or or_3 (c, jal, auipc, jalr, itype);
endmodule

module ALU_Controller (
  input  ALU_op_2,
  input  ALU_op_1,
  input  ALU_op_0,
  input  func_3_2,
  input  func_3_1,
  input  func_3_0,
  input  func_7,
  output a,
  output b,
  output c,
  output d
);

  wire and_1_out, and_2_out, and_3_out, and_4_out, and_5_out, and_6_out, and_7_out, and_8_out, and_9_out,
       and_10_out, and_11_out, and_12_out, and_13_out, and_14_out, and_15_out, and_16_out, and_17_out,
       and_18_out, and_19_out, and_20_out, not_1_out, not_2_out, not_3_out, not_4_out, not_5_out, not_6_out,
       not_7_out, not_8_out, not_9_out, not_10_out, not_11_out, not_12_out, not_13_out, not_14_out,
       not_15_out, not_16_out, not_17_out, not_18_out, not_19_out, not_20_out, not_21_out, not_22_out,
       not_23_out, not_24_out, not_25_out, not_26_out, not_27_out, not_28_out, not_29_out, not_30_out,
       not_31_out, not_32_out, not_33_out, not_34_out, not_35_out, not_36_out, not_37_out, not_38_out;

  not not_1 (not_1_out, ALU_op_2);
  not not_2 (not_2_out, func_3_1);
  not not_3 (not_3_out, ALU_op_2);
  not not_4 (not_4_out, ALU_op_2);
  not not_5 (not_5_out, ALU_op_1);
  not not_6 (not_6_out, func_3_2);
  not not_7 (not_7_out, ALU_op_2);
  not not_8 (not_8_out, ALU_op_0);
  not not_9 (not_9_out, ALU_op_2);
  not not_10 (not_10_out, ALU_op_1);
  not not_11 (not_11_out, func_3_1);
  not not_12 (not_12_out, func_3_0);
  not not_13 (not_13_out, func_7);
  not not_14 (not_14_out, ALU_op_2);
  not not_15 (not_15_out, func_3_1);
  not not_16 (not_16_out, func_3_0);
  not not_17 (not_17_out, ALU_op_2);
  not not_18 (not_18_out, func_3_2);
  not not_19 (not_19_out, ALU_op_2);
  not not_20 (not_20_out, ALU_op_0);
  not not_21 (not_21_out, func_3_0);
  not not_22 (not_22_out, ALU_op_2);
  not not_23 (not_23_out, func_3_0);
  not not_24 (not_24_out, ALU_op_2);
  not not_25 (not_25_out, ALU_op_2);
  not not_26 (not_26_out, ALU_op_2);
  not not_27 (not_27_out, ALU_op_0);
  not not_28 (not_28_out, func_3_1);
  not not_29 (not_29_out, ALU_op_2);
  not not_30 (not_30_out, func_3_2);
  not not_31 (not_31_out, func_3_1);
  not not_32 (not_32_out, ALU_op_2);
  not not_33 (not_33_out, func_3_1);
  not not_34 (not_34_out, ALU_op_2);
  not not_35 (not_35_out, ALU_op_1);
  not not_36 (not_36_out, func_3_0);
  and and_1 (and_1_out, not_1_out, func_3_2, not_2_out, func_3_0);
  and and_2 (and_2_out, not_3_out, ALU_op_1);
  and and_3 (and_3_out, ALU_op_1, ALU_op_0);
  not not_37 (not_37_out, ALU_op_2);
  and and_4 (and_4_out, not_37_out, not_38_out, func_3_0);
  not not_38 (not_38_out, func_3_2);
  and and_5 (and_5_out, not_4_out, not_5_out, not_6_out, func_3_1);
  and and_6 (and_6_out, not_7_out, not_8_out, func_3_1, func_3_0);
  and and_7 (and_7_out, not_9_out, not_10_out, func_3_2, not_11_out, not_12_out, not_13_out);
  and and_8 (and_8_out, not_14_out, ALU_op_0, func_3_2, not_15_out, not_16_out);
  and and_9 (and_9_out, ALU_op_1, ALU_op_0);
  and and_10 (and_10_out, not_17_out, not_18_out, func_3_0);
  and and_11 (and_11_out, not_19_out, not_20_out, func_3_2, not_21_out, func_7);
  and and_12 (and_12_out, not_22_out, func_3_2, func_3_1, not_23_out);
  and and_13 (and_13_out, not_24_out, ALU_op_0, func_3_1, func_3_0);
  and and_14 (and_14_out, not_25_out, ALU_op_1);
  and and_15 (and_15_out, ALU_op_1, ALU_op_0);
  and and_16 (and_16_out, not_26_out, not_27_out, not_28_out, func_7);
  and and_17 (and_17_out, not_29_out, not_30_out, not_31_out, func_3_0);
  and and_18 (and_18_out, not_32_out, not_33_out, func_3_0, func_7);
  and and_19 (and_19_out, not_34_out, not_35_out, func_3_1, not_36_out);
  and and_20 (and_20_out, ALU_op_1, ALU_op_0);
  or or_1 (a, and_1_out, and_2_out, and_3_out);
  or or_2 (c, and_10_out, and_11_out, and_12_out, and_13_out, and_14_out, and_15_out);
  or or_3 (d, and_16_out, and_17_out, and_18_out, and_19_out, and_20_out);
  or or_4 (b, and_4_out, and_5_out, and_6_out, and_7_out, and_8_out, and_9_out);
endmodule

module ALU (
  input  [3:0] in_1,
  input  [31:0] Operand_A,
  input  [31:0] Operand_B,
  output [31:0] Output
);

  wire comparator_1_lt, comparator_2_lt;
  wire [31:0] adder_1_out, and_1_out, multiplexer_1_out, multiplexer_2_out, or_1_out, shifter_1_out,
       shifter_2_out, shifter_3_out, subtractor_1_out, xor_1_out;

  Adder #(.width(32)) adder_1 (.a(Operand_A), .b(Operand_B), .out(adder_1_out));  // open: cin, cout
  Subtractor #(.width(32)) subtractor_1 (.a(Operand_A), .b(Operand_B), .out(subtractor_1_out));  // open: bin, bout
  assign and_1_out = Operand_A & Operand_B;  // AND_Gate and_1, 32 bits wide
  assign or_1_out = Operand_A | Operand_B;  // OR_Gate or_1, 32 bits wide
  assign xor_1_out = Operand_A ^ Operand_B;  // XOR_Gate xor_1, 32 bits wide
  Shifter #(.width(32)) shifter_1 (.in(Operand_A), .\dist (Operand_B[4:0]), .out(shifter_1_out));
  Shifter #(.width(32), .shift("lr")) shifter_2 (.in(Operand_A), .\dist (Operand_B[4:0]), .out(shifter_2_out));
  Comparator #(.width(32)) comparator_1 (.a(Operand_A), .b(Operand_B), .lt(comparator_1_lt));  // open: gt, eq
  Comparator #(.width(32), .mode("unsigned")) comparator_2 (
    .a(Operand_A), .b(Operand_B), .lt(comparator_2_lt));  // open: gt, eq
  Shifter #(.width(32), .shift("ar")) shifter_3 (.in(Operand_A), .\dist (Operand_B[4:0]), .out(shifter_3_out));
  Multiplexer #(.width(32), .enable("false")) multiplexer_1 (
    .in0({32{1'b0}}), .in1(32'h1), .out(multiplexer_1_out), .sel(comparator_1_lt));
  Multiplexer #(.width(32), .enable("false")) multiplexer_2 (
    .in0({32{1'b0}}), .in1(32'h1), .out(multiplexer_2_out), .sel(comparator_2_lt));
  Multiplexer #(.select(4), .width(32), .enable("false")) multiplexer_3 (
    .in0(adder_1_out), .in1(subtractor_1_out), .in2(and_1_out), .in3(or_1_out), .in4(xor_1_out),
    .in5(shifter_1_out), .in6(shifter_2_out), .in7(multiplexer_1_out), .in8(multiplexer_2_out),
    .in9(shifter_3_out), .in15(Operand_A), .out(Output), .sel(in_1));  // open: in10, in11, in12, in13, in14
endmodule

module Control_Unit (
  input  [6:0] Opcode,
  input  [2:0] in_2,
  input  in_3,
  output Write,
  output Branch,
  output Store,
  output Load,
  output [1:0] Operand_A,
  output Operand_B,
  output [1:0] Immediate,
  output [1:0] Next_PC,
  output [3:0] ALU_Operation
);

  wire type_decoder_1_i_type, type_decoder_1_i_type_2, type_decoder_1_i_type_3, type_decoder_1_r_type,
       type_decoder_1_s_type, type_decoder_1_sb_type, type_decoder_1_u_type, type_decoder_1_u_type_2,
       type_decoder_1_uj_type;

  Type_Decoder type_decoder_1 (
    .Instruction_Memory(Opcode), .R_Type(type_decoder_1_r_type), .I_Type(type_decoder_1_i_type),
    .I_Type_2(type_decoder_1_i_type_2), .I_Type_3(type_decoder_1_i_type_3), .S_Type(type_decoder_1_s_type),
    .SB_Type(type_decoder_1_sb_type), .U_Type(type_decoder_1_u_type), .U_Type_2(type_decoder_1_u_type_2),
    .UJ_Type(type_decoder_1_uj_type));
  Control_Decoder control_decoder_1 (
    .func_3(in_2), .func_7(in_3), .Write(Write), .Branch_2(Branch), .Store_2(Store), .Load_2(Load),
    .Operand_A(Operand_A), .Operand_B(Operand_B), .Immediate_Selector(Immediate), .Next_PC(Next_PC),
    .ALU_Operation_Selector(ALU_Operation), .R_Type(type_decoder_1_r_type), .I_Type(type_decoder_1_i_type_2),
    .Load(type_decoder_1_i_type), .JALR(type_decoder_1_i_type_3), .Store(type_decoder_1_s_type),
    .Branch(type_decoder_1_sb_type), .Auipc(type_decoder_1_u_type), .Lui(type_decoder_1_u_type_2),
    .JAL(type_decoder_1_uj_type));  // open: out_19
endmodule

module Branch_Selector (
  input  [31:0] Rs1,
  input  [31:0] Rs2,
  input  [2:0] in_3,
  output out_4
);

  wire comparator_1_eq, comparator_2_eq, comparator_3_lt, comparator_4_eq, comparator_4_gt, comparator_5_lt,
       comparator_6_eq, comparator_6_gt, not_1_out, or_1_out, or_2_out;

  Comparator #(.width(32)) comparator_1 (.a(Rs1), .b(Rs2), .eq(comparator_1_eq));  // open: gt, lt
  not not_1 (not_1_out, comparator_2_eq);
  Comparator #(.width(32)) comparator_2 (.a(Rs1), .b(Rs2), .eq(comparator_2_eq));  // open: gt, lt
  Comparator #(.width(32)) comparator_3 (.a(Rs1), .b(Rs2), .lt(comparator_3_lt));  // open: gt, eq
  Comparator #(.width(32)) comparator_4 (.a(Rs1), .b(Rs2), .gt(comparator_4_gt), .eq(comparator_4_eq));  // open: lt
  or or_1 (or_1_out, comparator_4_gt, comparator_4_eq);
  Comparator #(.width(32), .mode("unsigned")) comparator_5 (.a(Rs1), .b(Rs2), .lt(comparator_5_lt));  // open: gt, eq
  or or_2 (or_2_out, comparator_6_gt, comparator_6_eq);
  Comparator #(.width(32), .mode("unsigned")) comparator_6 (
    .a(Rs1), .b(Rs2), .gt(comparator_6_gt), .eq(comparator_6_eq));  // open: lt
  Multiplexer #(.select(3)) multiplexer_1 (
    .in0(comparator_1_eq), .in1(not_1_out), .in4(comparator_3_lt), .in5(or_1_out), .in6(comparator_5_lt),
    .in7(or_2_out), .out(out_4), .sel(in_3));  // open: in2, in3, en
endmodule

module ALU_Controller_cc (
  input  ALU_op_2,
  input  ALU_op_1,
  input  ALU_op_0,
  input  func_3_2,
  input  func_3_1,
  input  func_3_0,
  input  func_7,
  output a,
  output b,
  output c,
  output d
);

  wire and_1_out, and_2_out, and_3_out, and_4_out, and_5_out, and_6_out, and_7_out, and_8_out, and_9_out,
       and_10_out, and_11_out, and_12_out, and_13_out, and_14_out, and_15_out, and_16_out, and_17_out,
       and_18_out, and_19_out, and_20_out, and_21_out, and_22_out, and_23_out, and_24_out, and_25_out,
       and_26_out, and_27_out, and_28_out, and_29_out, and_30_out, and_31_out, and_32_out, and_33_out,
       and_34_out, and_35_out, and_36_out, and_37_out, and_38_out, and_39_out, and_40_out, and_41_out,
       and_42_out, and_43_out, and_44_out, and_45_out, and_46_out, and_47_out, and_48_out, and_49_out,
       and_50_out, not_1_out, not_2_out, not_3_out, not_4_out, not_5_out, not_6_out, not_7_out, not_8_out,
       not_9_out, not_10_out, not_11_out, not_12_out, not_13_out, not_14_out, not_15_out, not_16_out,
       not_17_out, not_18_out, not_19_out, not_20_out, not_21_out, not_22_out, not_23_out, not_24_out,
       not_25_out, not_26_out, not_27_out, not_28_out, not_29_out, not_30_out, not_31_out, not_32_out,
       not_33_out, not_34_out, not_35_out, not_36_out, not_37_out, not_38_out, not_39_out, or_1_out,
       or_2_out, or_3_out, or_4_out, or_6_out, or_7_out, or_8_out, or_9_out, or_10_out, or_11_out, or_13_out,
       or_14_out;

  not not_1 (not_1_out, ALU_op_2);
  not not_2 (not_2_out, func_3_1);
  not not_3 (not_3_out, ALU_op_2);
  not not_4 (not_4_out, ALU_op_2);
  not not_5 (not_5_out, ALU_op_2);
  not not_6 (not_6_out, func_3_2);
  not not_7 (not_7_out, ALU_op_2);
  not not_8 (not_8_out, ALU_op_1);
  not not_9 (not_9_out, func_3_2);
  not not_10 (not_10_out, ALU_op_2);
  not not_11 (not_11_out, ALU_op_1);
  not not_12 (not_12_out, func_3_1);
  not not_13 (not_13_out, func_3_0);
  not not_14 (not_14_out, ALU_op_2);
  not not_15 (not_15_out, ALU_op_2);
  not not_16 (not_16_out, ALU_op_0);
  not not_17 (not_17_out, ALU_op_2);
  not not_18 (not_18_out, ALU_op_0);
  not not_19 (not_19_out, func_3_1);
  not not_20 (not_20_out, ALU_op_2);
  not not_21 (not_21_out, func_3_2);
  not not_22 (not_22_out, func_3_1);
  and and_1 (and_1_out, not_1_out, func_3_2);
  and and_2 (and_2_out, not_2_out, func_3_0);
  and and_3 (and_3_out, not_3_out, ALU_op_1);
  not not_23 (not_23_out, func_3_2);
  and and_4 (and_4_out, not_4_out, ALU_op_1);
  not not_24 (not_24_out, func_3_0);
  and and_5 (and_5_out, not_5_out, not_6_out);
  and and_6 (and_6_out, not_7_out, not_8_out);
  and and_7 (and_7_out, not_9_out, func_3_1);
  and and_8 (and_8_out, not_10_out, not_11_out);
  and and_9 (and_9_out, not_12_out, not_13_out);
  not not_25 (not_25_out, func_7);
  and and_10 (and_10_out, not_14_out, ALU_op_0);
  not not_26 (not_26_out, func_3_1);
  not not_27 (not_27_out, func_3_0);
  not not_28 (not_28_out, ALU_op_2);
  not not_29 (not_29_out, func_3_2);
  and and_11 (and_11_out, not_15_out, not_16_out);
  not not_30 (not_30_out, func_3_0);
  not not_31 (not_31_out, ALU_op_2);
  and and_12 (and_12_out, not_17_out, not_18_out);
  and and_13 (and_13_out, not_19_out, func_7);
  and and_14 (and_14_out, not_20_out, not_21_out);
  and and_15 (and_15_out, not_22_out, func_3_0);
  not not_32 (not_32_out, ALU_op_2);
  not not_33 (not_33_out, func_3_1);
  not not_34 (not_34_out, ALU_op_2);
  not not_35 (not_35_out, ALU_op_1);
  not not_36 (not_36_out, func_3_0);
  and and_16 (and_16_out, and_1_out, and_2_out);
  and and_17 (and_17_out, and_3_out, not_23_out);
  and and_18 (and_18_out, and_4_out, not_24_out);
  and and_19 (and_19_out, ALU_op_1, ALU_op_0);
  and and_20 (and_20_out, and_5_out, func_3_0);
  and and_21 (and_21_out, and_6_out, and_7_out);
  and and_22 (and_22_out, and_8_out, func_3_2);
  and and_23 (and_23_out, and_9_out, not_25_out);
  and and_24 (and_24_out, and_10_out, func_3_2);
  and and_25 (and_25_out, not_26_out, not_27_out);
  and and_26 (and_26_out, not_28_out, not_29_out);
  and and_27 (and_27_out, and_11_out, func_3_2);
  and and_28 (and_28_out, not_30_out, func_7);
  not not_37 (not_37_out, ALU_op_2);
  not not_38 (not_38_out, func_7);
  and and_29 (and_29_out, not_31_out, ALU_op_0);
  and and_30 (and_30_out, func_3_2, func_3_1);
  not not_39 (not_39_out, ALU_op_2);
  and and_31 (and_31_out, and_12_out, and_13_out);
  and and_32 (and_32_out, and_14_out, and_15_out);
  and and_33 (and_33_out, not_32_out, not_33_out);
  and and_34 (and_34_out, func_3_0, func_7);
  and and_35 (and_35_out, not_34_out, not_35_out);
  and and_36 (and_36_out, func_3_1, not_36_out);
  or or_1 (or_1_out, and_16_out, and_17_out);
  or or_2 (or_2_out, and_18_out, and_19_out);
  or or_3 (or_3_out, and_20_out, and_21_out);
  and and_37 (and_37_out, and_22_out, and_23_out);
  and and_38 (and_38_out, and_24_out, and_25_out);
  and and_39 (and_39_out, ALU_op_1, ALU_op_0);
  and and_40 (and_40_out, and_26_out, func_3_0);
  and and_41 (and_41_out, and_27_out, and_28_out);
  and and_42 (and_42_out, not_37_out, func_3_2);
  and and_43 (and_43_out, func_3_1, not_38_out);
  and and_44 (and_44_out, and_29_out, and_30_out);
  and and_45 (and_45_out, not_39_out, ALU_op_1);
  or or_4 (or_4_out, and_31_out, and_32_out);
  and and_46 (and_46_out, and_33_out, and_34_out);
  and and_47 (and_47_out, and_35_out, and_36_out);
  and and_48 (and_48_out, ALU_op_1, ALU_op_0);
  or or_5 (a, or_1_out, or_2_out);
  or or_6 (or_6_out, or_3_out, and_37_out);
  or or_7 (or_7_out, and_38_out, and_39_out);
  or or_8 (or_8_out, and_40_out, and_41_out);
  and and_49 (and_49_out, and_42_out, and_43_out);
  or or_9 (or_9_out, and_44_out, and_45_out);
  and and_50 (and_50_out, ALU_op_1, ALU_op_0);
  or or_10 (or_10_out, or_4_out, and_46_out);
  or or_11 (or_11_out, and_47_out, and_48_out);
  or or_12 (b, or_6_out, or_7_out);
  or or_13 (or_13_out, or_8_out, and_49_out);
  or or_14 (or_14_out, or_9_out, and_50_out);
  or or_15 (d, or_10_out, or_11_out);
  or or_16 (c, or_13_out, or_14_out);
endmodule

module ALU_Controller_5 (
  input  ALU_op_2,
  input  ALU_op_1,
  input  ALU_op_0,
  input  func_7,
  input  fun3_2,
  input  fun3_1,
  input  fun3_0,
  output a,
  output b,
  output c,
  output d
);

  wire and_1_out, and_2_out, and_3_out, and_4_out, and_5_out, and_6_out, and_7_out, and_8_out, and_9_out,
       and_10_out, and_11_out, and_12_out, and_13_out, and_14_out, and_15_out, and_16_out, and_17_out,
       and_18_out, and_19_out, and_20_out, and_21_out, and_22_out, and_23_out, and_24_out, and_25_out,
       and_26_out, and_27_out, and_28_out, and_29_out, and_30_out, and_31_out, and_32_out, and_33_out,
       and_34_out, and_35_out, and_36_out, and_37_out, and_38_out, and_39_out, and_40_out, not_1_out,
       not_2_out, not_3_out, not_4_out, not_5_out, not_6_out, not_7_out, not_8_out, not_9_out, not_10_out,
       not_11_out, not_12_out, not_13_out, not_14_out, not_15_out, not_16_out, not_17_out, not_18_out,
       not_19_out, not_20_out, not_21_out, not_22_out, not_23_out, not_24_out, not_25_out, not_26_out,
       not_27_out, not_28_out, not_29_out, not_30_out, not_31_out, or_1_out, or_2_out, or_3_out, or_4_out,
       or_6_out, or_7_out, or_9_out, or_10_out;

  not not_1 (not_1_out, ALU_op_2);
  not not_2 (not_2_out, fun3_2);
  not not_3 (not_3_out, ALU_op_2);
  not not_4 (not_4_out, fun3_1);
  not not_5 (not_5_out, ALU_op_2);
  not not_6 (not_6_out, ALU_op_0);
  not not_7 (not_7_out, ALU_op_2);
  not not_8 (not_8_out, ALU_op_0);
  not not_9 (not_9_out, fun3_0);
  not not_10 (not_10_out, ALU_op_2);
  not not_11 (not_11_out, func_7);
  not not_12 (not_12_out, ALU_op_2);
  not not_13 (not_13_out, ALU_op_2);
  not not_14 (not_14_out, fun3_2);
  not not_15 (not_15_out, fun3_1);
  not not_16 (not_16_out, ALU_op_2);
  not not_17 (not_17_out, ALU_op_0);
  not not_18 (not_18_out, fun3_0);
  and and_1 (and_1_out, not_1_out, not_2_out);
  and and_2 (and_2_out, fun3_1, fun3_0);
  and and_3 (and_3_out, not_3_out, func_7);
  and and_4 (and_4_out, not_4_out, fun3_0);
  not not_19 (not_19_out, ALU_op_2);
  not not_20 (not_20_out, func_7);
  not not_21 (not_21_out, fun3_1);
  and and_5 (and_5_out, not_5_out, not_6_out);
  not not_22 (not_22_out, fun3_2);
  not not_23 (not_23_out, fun3_0);
  not not_24 (not_24_out, ALU_op_2);
  not not_25 (not_25_out, fun3_1);
  not not_26 (not_26_out, fun3_0);
  and and_6 (and_6_out, not_7_out, not_8_out);
  and and_7 (and_7_out, fun3_1, not_9_out);
  and and_8 (and_8_out, not_10_out, not_11_out);
  and and_9 (and_9_out, fun3_2, fun3_0);
  and and_10 (and_10_out, not_12_out, fun3_2);
  and and_11 (and_11_out, not_13_out, not_14_out);
  and and_12 (and_12_out, not_15_out, fun3_0);
  and and_13 (and_13_out, not_16_out, not_17_out);
  and and_14 (and_14_out, fun3_1, not_18_out);
  not not_27 (not_27_out, ALU_op_1);
  not not_28 (not_28_out, ALU_op_0);
  not not_29 (not_29_out, fun3_1);
  not not_30 (not_30_out, ALU_op_2);
  not not_31 (not_31_out, fun3_1);
  and and_15 (and_15_out, and_1_out, and_2_out);
  and and_16 (and_16_out, and_3_out, and_4_out);
  and and_17 (and_17_out, not_19_out, not_20_out);
  and and_18 (and_18_out, not_21_out, fun3_0);
  and and_19 (and_19_out, and_5_out, not_22_out);
  and and_20 (and_20_out, fun3_1, not_23_out);
  and and_21 (and_21_out, not_24_out, fun3_2);
  and and_22 (and_22_out, not_25_out, not_26_out);
  and and_23 (and_23_out, and_6_out, and_7_out);
  and and_24 (and_24_out, and_8_out, and_9_out);
  and and_25 (and_25_out, and_10_out, fun3_1);
  and and_26 (and_26_out, ALU_op_1, ALU_op_0);
  and and_27 (and_27_out, and_11_out, and_12_out);
  and and_28 (and_28_out, and_13_out, and_14_out);
  and and_29 (and_29_out, not_27_out, not_28_out);
  and and_30 (and_30_out, func_7, not_29_out);
  and and_31 (and_31_out, not_30_out, func_7);
  and and_32 (and_32_out, not_31_out, fun3_0);
  or or_1 (or_1_out, and_15_out, and_16_out);
  and and_33 (and_33_out, ALU_op_1, ALU_op_0);
  and and_34 (and_34_out, and_17_out, and_18_out);
  and and_35 (and_35_out, and_19_out, and_20_out);
  and and_36 (and_36_out, and_21_out, and_22_out);
  and and_37 (and_37_out, ALU_op_1, ALU_op_0);
  or or_2 (or_2_out, and_23_out, and_24_out);
  or or_3 (or_3_out, and_25_out, and_26_out);
  or or_4 (or_4_out, and_27_out, and_28_out);
  and and_38 (and_38_out, and_29_out, and_30_out);
  and and_39 (and_39_out, and_31_out, and_32_out);
  and and_40 (and_40_out, ALU_op_1, ALU_op_0);
  or or_5 (a, or_1_out, and_33_out);
  or or_6 (or_6_out, and_34_out, and_35_out);
  or or_7 (or_7_out, and_36_out, and_37_out);
  or or_8 (c, or_2_out, or_3_out);
  or or_9 (or_9_out, or_4_out, and_38_out);
  or or_10 (or_10_out, and_39_out, and_40_out);
  or or_11 (b, or_6_out, or_7_out);
  or or_12 (d, or_9_out, or_10_out);
endmodule

module ALU_Operation_Selector_1 (
  input  Rtype,
  input  itype,
  input  load,
  input  jalr,
  input  store,
  input  auipc,
  input  lui,
  input  jal,
  output a,
  output b,
  output c
);

  wire and_1_out, and_2_out, and_3_out, and_4_out, and_5_out, and_6_out, and_7_out, and_8_out, and_9_out,
       and_10_out, and_11_out, and_12_out, not_1_out, not_2_out, not_3_out, not_4_out, not_5_out, not_6_out,
       or_1_out, or_2_out, or_4_out, or_5_out, or_6_out, or_7_out, or_8_out, or_9_out, or_10_out, or_11_out,
       or_12_out, or_13_out;

  or or_1 (or_1_out, jal, lui);
  or or_2 (or_2_out, auipc, store);
  not not_1 (not_1_out, Rtype);
  and and_1 (and_1_out, not_1_out, itype);
  not not_2 (not_2_out, store);
  and and_2 (and_2_out, not_2_out, not_3_out);
  not not_3 (not_3_out, auipc);
  not not_4 (not_4_out, Rtype);
  and and_3 (and_3_out, not_4_out, load);
  not not_5 (not_5_out, store);
  and and_4 (and_4_out, not_5_out, not_6_out);
  not not_6 (not_6_out, lui);
  or or_3 (a, or_1_out, or_2_out);
  and and_5 (and_5_out, load, auipc);
  and and_6 (and_6_out, load, store);
  and and_7 (and_7_out, and_1_out, and_2_out);
  and and_8 (and_8_out, and_3_out, and_4_out);
  and and_9 (and_9_out, itype, lui);
  and and_10 (and_10_out, itype, store);
  or or_4 (or_4_out, jal, lui);
  or or_5 (or_5_out, jalr, and_5_out);
  or or_6 (or_6_out, and_6_out, and_7_out);
  and and_11 (and_11_out, Rtype, load);
  or or_7 (or_7_out, jal, auipc);
  or or_8 (or_8_out, jalr, and_8_out);
  or or_9 (or_9_out, and_9_out, and_10_out);
  and and_12 (and_12_out, Rtype, itype);
  or or_10 (or_10_out, or_4_out, or_5_out);
  or or_11 (or_11_out, or_6_out, and_11_out);
  or or_12 (or_12_out, or_7_out, or_8_out);
  or or_13 (or_13_out, or_9_out, and_12_out);
  or or_14 (b, or_10_out, or_11_out);
  or or_15 (c, or_12_out, or_13_out);
endmodule
